// Logisim project Moore_Machine.circ as structural Verilog: 1 circuit, main circuit main
module main (
  input  in_1,
  output Z1,
  output Z2
);

  wire and_1_out, and_2_out, and_3_out, and_4_out, and_5_out, and_6_out, and_7_out, and_8_out, and_9_out,
       and_10_out, and_11_out, and_12_out, clock_1_out, j_k_ff_1_q, j_k_ff_1_qn, j_k_ff_2_q, j_k_ff_2_qn,
       j_k_ff_3_q, j_k_ff_3_qn, not_1_out, or_1_out, or_2_out, or_3_out, or_4_out, or_5_out;

  not not_1 (not_1_out, in_1);
  and and_1 (and_1_out, j_k_ff_2_qn, not_1_out);
  and and_2 (and_2_out, j_k_ff_2_q, j_k_ff_3_q);
  and and_3 (and_3_out, j_k_ff_1_q, in_1);
  and and_4 (and_4_out, j_k_ff_3_q, not_1_out);
  and and_5 (and_5_out, j_k_ff_1_q, j_k_ff_3_q, not_1_out);
  and and_6 (and_6_out, in_1, j_k_ff_3_q, j_k_ff_1_qn);
  and and_7 (and_7_out, not_1_out, j_k_ff_3_qn, j_k_ff_1_qn);
  and and_8 (and_8_out, in_1, j_k_ff_2_qn, j_k_ff_1_qn);
  and and_9 (and_9_out, not_1_out, j_k_ff_1_q, j_k_ff_2_q);
  and and_10 (and_10_out, j_k_ff_2_qn, j_k_ff_1_q);
  and and_11 (and_11_out, j_k_ff_2_q, j_k_ff_1_qn);
  or or_1 (or_1_out, and_8_out, and_9_out);
  Clock clock_1 (.out(clock_1_out));
  and and_12 (and_12_out, in_1, j_k_ff_3_q);
  or or_2 (or_2_out, and_1_out, and_2_out);
  or or_3 (or_3_out, and_3_out, and_4_out);
  or or_4 (or_4_out, and_5_out, and_6_out, and_7_out);
  or or_5 (or_5_out, and_10_out, and_11_out, not_1_out);
  J_K_Flip_Flop j_k_ff_1 (
    .J(and_12_out), .K(or_2_out), .clk(clock_1_out), .Q(j_k_ff_1_q), .Qn(j_k_ff_1_qn));  // open: preset, reset
  J_K_Flip_Flop j_k_ff_2 (
    .J(or_3_out), .K(or_4_out), .clk(clock_1_out), .Q(j_k_ff_2_q), .Qn(j_k_ff_2_qn));  // open: preset, reset
  J_K_Flip_Flop j_k_ff_3 (
    .J(or_1_out), .K(or_5_out), .clk(clock_1_out), .Q(j_k_ff_3_q), .Qn(j_k_ff_3_qn));  // open: preset, reset
  and and_13 (Z1, j_k_ff_1_q, j_k_ff_2_q, j_k_ff_3_q);
  and and_14 (Z2, j_k_ff_2_qn, j_k_ff_1_q, j_k_ff_3_qn);

  // Notes on the sheet:
  //   J2
  //   J1
  //   J0
endmodule
